// Logisim project LC-3.circ as structural Verilog: 4 circuits, main circuit main
module main (
  output [15:0] out_1,
  output [2:0] dst,
  output [2:0] src1,
  output [2:0] src2,
  output [15:0] out_5,
  output [15:0] out_6,
  output [15:0] out_7,
  output [15:0] out_8
);

  wire aAND_out, ADD_out, and_1_out, and_2_out, and_3_out, BR, clck, decode, evalAdd, exeOp, fetch, fetchOp,
       LD, LDR, multiplexer_7_out, nNOT_out, not_1_out, not_2_out, not_3_out, not_4_out, not_5_out,
       not_6_out, not_7_out, not_8_out, not_9_out, not_10_out, not_11_out, not_12_out, not_13_out,
       not_14_out, not_15_out, not_16_out, not_17_out, or_1_out, or_2_out, or_3_out, or_4_out, or_5_out,
       RAMtoReg, ST, store, STR, write;
  wire [15:0] adder_1_out, alu_1_result, baseReg, bit_extender_1_out, bit_extender_2_out, instruc,
       multiplexer_1_out, multiplexer_2_out, multiplexer_6_out;

  Clock u_clck (.out(clck));
  or or_1 (or_1_out, STR, LDR);
  assign bit_extender_1_out = {{7{instruc[8]}}, instruc[8:0]};  // Bit_Extender bit_extender_1
  assign bit_extender_2_out = {{10{instruc[5]}}, instruc[5:0]};  // Bit_Extender bit_extender_2
  Multiplexer #(.width(16), .enable("false")) multiplexer_1 (
    .in0(out_5), .in1(baseReg), .out(multiplexer_1_out), .sel(or_1_out));
  Multiplexer #(.width(16), .enable("false")) multiplexer_2 (
    .in0(bit_extender_1_out), .in1(bit_extender_2_out), .out(multiplexer_2_out), .sel(or_2_out));
  or or_2 (or_2_out, LDR, STR);
  or or_3 (or_3_out, LD, LDR, STR, ST);
  Multiplexer #(.width(3), .enable("false")) multiplexer_3 (
    .in0(instruc[2:0]), .in1(instruc[8:6]), .out(src2), .sel(BR));
  Adder #(.width(16)) adder_1 (.a(multiplexer_1_out), .b(multiplexer_2_out), .out(adder_1_out));  // open: cin, cout
  and and_1 (and_1_out, or_3_out, not_1_out);
  not not_1 (not_1_out, store);
  Multiplexer #(.width(3), .enable("false")) multiplexer_4 (.in0(instruc[8:6]), .in1(dst), .out(src1), .sel(write));
  Multiplexer #(.width(16), .enable("false")) multiplexer_5 (
    .in0(out_5), .in1(adder_1_out), .out(out_6), .sel(and_1_out));
  and and_2 (and_2_out, exeOp, write);
  not not_2 (not_2_out, write);
  or or_4 (or_4_out, exeOp, fetch);
  and and_3 (and_3_out, not_2_out, exeOp);
  RAM #(.addrWidth(16), .dataWidth(16), .databus("bibus")) ram_1 (
    .addr(out_6), .we(and_2_out), .oe(or_4_out), .clk(clck), .din(out_8), .dout(out_7));
  registers registers_1 (
    .clock(clck), .dstReg(dst), .dstVal(out_1), .srcReg1(src1), .srcReg2(src2), .WE(and_3_out),
    .srcReg1Val(out_8), .srcReg2Val(baseReg));
  controlUnit controlunit_1 (
    .IRin(out_7), .clock(clck), .PCin(out_8), .fetch(fetch), .decodeInstruction(decode), .evalAdd(evalAdd),
    .instruction({instruc[15:12], dst, instruc[8:0]}), .fetchOpfromMem(fetchOp), .exeOp(exeOp),
    .PCout(out_5), .store(store));
  Multiplexer #(.width(16), .enable("false")) multiplexer_6 (
    .in0({16{1'b0}}), .in1({instruc[15:12], dst, instruc[8:0]}), .out(multiplexer_6_out),
    .sel(multiplexer_7_out));
  Multiplexer #(.enable("false")) multiplexer_7 (.in0(1'b0), .in1(exeOp), .out(multiplexer_7_out), .sel(or_5_out));
  Multiplexer #(.width(16), .enable("false")) multiplexer_8 (
    .in0(alu_1_result), .in1(out_7), .out(out_1), .sel(RAMtoReg));
  alu alu_1 (.RegA(out_8), .RegB(baseReg), .Instruction(multiplexer_6_out), .result(alu_1_result));
  and ADD (ADD_out, not_4_out, not_3_out, not_6_out, instruc[12]);
  not not_3 (not_3_out, instruc[14]);
  not not_4 (not_4_out, instruc[15]);
  or or_5 (or_5_out, nNOT_out, aAND_out, ADD_out);
  and aAND (aAND_out, not_5_out, instruc[14], not_7_out, instruc[12]);
  not not_5 (not_5_out, instruc[15]);
  not not_6 (not_6_out, instruc[13]);
  not not_7 (not_7_out, instruc[13]);
  and nNOT (nNOT_out, instruc[15], not_9_out, not_10_out, instruc[12]);
  not not_8 (not_8_out, instruc[15]);
  not not_9 (not_9_out, instruc[14]);
  not not_10 (not_10_out, instruc[13]);
  or or_6 (RAMtoReg, LD, LDR);
  and u_ST (ST, not_14_out, not_13_out, instruc[13], instruc[12]);
  and u_LD (LD, not_8_out, not_11_out, instruc[13], not_12_out);
  not not_11 (not_11_out, instruc[14]);
  not not_12 (not_12_out, instruc[12]);
  not not_13 (not_13_out, instruc[14]);
  not not_14 (not_14_out, instruc[15]);
  or or_7 (write, ST, STR);
  and u_LDR (LDR, not_15_out, instruc[14], instruc[13], not_16_out);
  not not_15 (not_15_out, instruc[15]);
  not not_16 (not_16_out, instruc[12]);
  or or_8 (BR, LDR, STR);
  and u_STR (STR, not_17_out, instruc[14], instruc[13], instruc[12]);
  not not_17 (not_17_out, instruc[15]);

  // Other names for the same wires on the sheet: instruc[11:9] = dst; src1RegIn[15:0] = out_8; RAMtoPC[15:0] = out_7;
  //   toReg[15:0] = out_7

  // Notes on the sheet:
  //   out_7: pull=down
  //   out_1: pull=down
  //   out_8: pull=down
endmodule

module controlUnit (
  input  [15:0] IRin,
  input  clock,
  input  [15:0] PCin,
  output fetch,
  output decodeInstruction,
  output evalAdd,
  output [15:0] instruction,
  output fetchOpfromMem,
  output exeOp,
  output [15:0] PCout,
  output store
);

  wire and_1_out, not_1_out, not_2_out, not_3_out;
  wire [2:0] programCnt_q;
  wire [15:0] adder_1_out, multiplexer_1_out;

  Counter #(.width(3), .max('h7)) programCnt (.clk(clock), .Q(programCnt_q));  // open: clr, load, up, count, D, carry
  Register #(.width(16), .trigger("falling")) InstructionReegister (
    .D(IRin), .en(fetch), .clk(clock), .Q(instruction));  // open: clr
  Adder #(.width(16)) adder_1 (.a(PCout), .b(16'h1), .out(adder_1_out));  // open: cin, cout
  Multiplexer #(.width(16), .enable("false")) multiplexer_1 (
    .in0(adder_1_out), .in1(PCin), .out(multiplexer_1_out), .sel(and_1_out));
  and and_1 (and_1_out, instruction[15], instruction[14]);
  Register #(.width(16)) PC (.D(multiplexer_1_out), .en(decodeInstruction), .clk(clock), .Q(PCout));  // open: clr
  not not_1 (not_1_out, programCnt_q[0]);
  not not_2 (not_2_out, programCnt_q[1]);
  not not_3 (not_3_out, programCnt_q[2]);
  and and_2 (store, not_1_out, not_2_out, not_3_out);
  D_Flip_Flop d_ff_1 (.D(store), .clk(clock), .Q(fetch));  // open: Qn, preset, reset
  D_Flip_Flop d_ff_2 (.D(fetch), .clk(clock), .Q(decodeInstruction));  // open: Qn, preset, reset
  D_Flip_Flop d_ff_3 (.D(decodeInstruction), .clk(clock), .Q(evalAdd));  // open: Qn, preset, reset
  D_Flip_Flop d_ff_4 (.D(evalAdd), .clk(clock), .Q(fetchOpfromMem));  // open: Qn, preset, reset
  D_Flip_Flop d_ff_5 (.D(fetchOpfromMem), .clk(clock), .Q(exeOp));  // open: Qn, preset, reset
  D_Flip_Flop d_ff_6 (.D(exeOp), .clk(clock));  // open: Q, Qn, preset, reset

  // Other names for the same wires on the sheet: decode = decodeInstruction; phase000 = store

  // Notes on the sheet:
  //   IRin: pull=down
  //   instruction: pull=down
endmodule

module alu (
  input  [15:0] RegA,
  input  [15:0] RegB,
  input  [15:0] Instruction,
  output [15:0] result
);

  wire [15:0] adder_1_out, and_1_out, bit_extender_1_out, multiplexer_1_out, not_1_out;

  assign bit_extender_1_out = {{11{Instruction[4]}}, Instruction[4:0]};  // Bit_Extender bit_extender_1
  Multiplexer #(.width(16), .enable("false")) multiplexer_1 (
    .in0(RegB), .in1(bit_extender_1_out), .out(multiplexer_1_out), .sel(Instruction[5]));
  Adder #(.width(16)) adder_1 (.a(RegA), .b(multiplexer_1_out), .out(adder_1_out));  // open: cin, cout
  assign and_1_out = RegA & multiplexer_1_out;  // AND_Gate and_1, 16 bits wide
  assign not_1_out = ~RegA;  // NOT_Gate not_1, 16 bits wide
  Multiplexer #(.select(2), .width(16), .enable("false")) multiplexer_2 (
    .in0(adder_1_out), .in1(and_1_out), .in2(not_1_out), .out(result), .sel(Instruction[15:14]));  // open: in3
endmodule

module registers (
  input  clock,
  input  [2:0] dstReg,
  input  [15:0] dstVal,
  input  [2:0] srcReg1,
  input  [2:0] srcReg2,
  input  WE,
  output [15:0] srcReg1Val,
  output [15:0] srcReg2Val
);

  wire demultiplexer_1_out0, demultiplexer_1_out1, demultiplexer_1_out2, demultiplexer_1_out3,
       demultiplexer_1_out4, demultiplexer_1_out5, demultiplexer_1_out6, demultiplexer_1_out7;
  wire [15:0] R0_q, R1_q, R2_q, R3_q, R4_q, R5_q, R6_q, R7_q;

  Demultiplexer #(.select(3), .enable("false")) demultiplexer_1 (
    .out0(demultiplexer_1_out0), .out1(demultiplexer_1_out1), .out2(demultiplexer_1_out2),
    .out3(demultiplexer_1_out3), .out4(demultiplexer_1_out4), .out5(demultiplexer_1_out5),
    .out6(demultiplexer_1_out6), .out7(demultiplexer_1_out7), .in(WE), .sel(dstReg));
  Register #(.width(16)) R0 (.D(dstVal), .en(demultiplexer_1_out0), .clk(clock), .Q(R0_q));  // open: clr
  Register #(.width(16)) R2 (.D(dstVal), .en(demultiplexer_1_out2), .clk(clock), .Q(R2_q));  // open: clr
  Register #(.width(16)) R4 (.D(dstVal), .en(demultiplexer_1_out4), .clk(clock), .Q(R4_q));  // open: clr
  Register #(.width(16)) R6 (.D(dstVal), .en(demultiplexer_1_out6), .clk(clock), .Q(R6_q));  // open: clr
  Register #(.width(16)) R1 (.D(dstVal), .en(demultiplexer_1_out1), .clk(clock), .Q(R1_q));  // open: clr
  Register #(.width(16)) R3 (.D(dstVal), .en(demultiplexer_1_out3), .clk(clock), .Q(R3_q));  // open: clr
  Register #(.width(16)) R5 (.D(dstVal), .en(demultiplexer_1_out5), .clk(clock), .Q(R5_q));  // open: clr
  Register #(.width(16)) R7 (.D(dstVal), .en(demultiplexer_1_out7), .clk(clock), .Q(R7_q));  // open: clr
  Multiplexer #(.select(3), .width(16), .enable("false")) multiplexer_1 (
    .in0(R0_q), .in1(R1_q), .in2(R2_q), .in3(R3_q), .in4(R4_q), .in5(R5_q), .in6(R6_q), .in7(R7_q),
    .out(srcReg1Val), .sel(srcReg1));
  Multiplexer #(.select(3), .width(16), .enable("false")) multiplexer_2 (
    .in0(R0_q), .in1(R1_q), .in2(R2_q), .in3(R3_q), .in4(R4_q), .in5(R5_q), .in6(R6_q), .in7(R7_q),
    .out(srcReg2Val), .sel(srcReg2));
endmodule
